# Fritzing sketch Litar Kawal Servo Motor dan LED Menggunakan Rotary Encoder (saved by Fritzing 0.9.2b)
breadboards: 1

parts:
  RE1 = KY-040 Rotary encoder [package=THT]
  LED2 = smd LED [color="Red (633nm)" package="0805 [SMD]"]
  R1 = Resistor [tolerance=±5% resistance=220 package="2010 [SMD]"]
  Part1 = Arduino Uno (Rev3) - ICSP

nets:
  GND: RE1.GND, LED2.cathode, Part1.GND
  VCC: RE1.Vcc, Part1.5V
  N1: RE1.SW, Part1.D11_PWM/MOSI
  N2: RE1.DT, Part1.D3_PWM
  N3: RE1.CLK, Part1.D2
  N4: LED2.anode, R1.Pin_1
  N5: R1.Pin_0, Part1.D4

custom parts:
  KY-040 Rotary encoder: KY-040 Rotary Encoder with switch on breakout borad from AZ Delivery
